// Logisim project cpu_design.circ as structural Verilog: 4 circuits, main circuit main
module main (
  input  [7:0] in_1,
  input  [7:0] in_2,
  input  in_3
);

  wire clock_1_out;

  Register register_1 (.D(in_2), .en(in_3), .Q(in_1), .clk(clock_1_out));  // open: clr
  Clock clock_1 (.out(clock_1_out));

  // Notes on the sheet:
  //   register a
endmodule

// au
module AU (
  input  [7:0] input_b,
  input  [7:0] input_a,
  input  mode_sub_add,
  output C_OUT,
  output [7:0] \output ,
  output z_flag,
  output overflow_flag
);

  wire xnor_1_out, xor_2_out;
  wire [7:0] bit_extender_1_out, xor_1_out;

  assign bit_extender_1_out = {{7{mode_sub_add}}, mode_sub_add};  // Bit_Extender bit_extender_1
  assign xor_1_out = input_b ^ bit_extender_1_out;  // XOR_Gate xor_1, 8 bits wide
  xor xor_2 (xor_2_out, \output [7], input_b[7]);
  xnor xnor_1 (xnor_1_out, input_b[7], input_a[7]);
  Adder adder_1 (.a(input_a), .b(xor_1_out), .out(\output ), .cin(mode_sub_add), .cout(C_OUT));
  and and_1 (overflow_flag, xor_2_out, xnor_1_out);
  Comparator comparator_1 (.a(\output ), .b({8{1'b0}}), .eq(z_flag));  // open: gt, lt
endmodule

module LU (
  input  [7:0] input_a,
  input  [7:0] input_b,
  input  _1,
  input  _2,
  output [7:0] \output 
);

  wire [7:0] and_1_out, not_1_out, or_1_out, xor_1_out;

  assign xor_1_out = input_a ^ input_b;  // XOR_Gate xor_1, 8 bits wide
  assign or_1_out = input_a | input_b;  // OR_Gate or_1, 8 bits wide
  assign and_1_out = input_a & input_b;  // AND_Gate and_1, 8 bits wide
  assign not_1_out = ~input_a;  // NOT_Gate not_1, 8 bits wide
  Multiplexer #(.select(2), .width(8), .enable("false")) multiplexer_1 (
    .in0(xor_1_out), .in1(or_1_out), .in2(and_1_out), .in3(not_1_out), .out(\output ), .sel({_1, _2}));
endmodule

module ALU_Final (
  input  [3:0] Opcode,
  input  carry_flag,
  input  [7:0] input_a,
  input  z_flag,
  input  overflow_flag,
  input  in_6,
  input  [7:0] input_b,
  output [7:0] out_8
);

  wire [7:0] arthmetic_unit_output, logic_unit_output, multiplexer_1_out, multiplexer_2_out, not_1_out,
       not_2_out;

  assign not_1_out = ~input_a;  // NOT_Gate not_1, 8 bits wide
  assign not_2_out = ~input_b;  // NOT_Gate not_2, 8 bits wide
  Multiplexer #(.width(8)) multiplexer_1 (
    .in0(input_a), .in1(not_1_out), .out(multiplexer_1_out), .sel(Opcode[0]));  // open: en
  Multiplexer #(.width(8)) multiplexer_2 (
    .in0(input_b), .in1(not_2_out), .out(multiplexer_2_out), .sel(Opcode[1]));  // open: en
  AU arthmetic_unit (
    .input_b(multiplexer_2_out), .input_a(multiplexer_1_out), .mode_sub_add(Opcode[2]), .C_OUT(carry_flag),
    .\output (arthmetic_unit_output), .z_flag(z_flag), .overflow_flag(overflow_flag));
  LU logic_unit (
    .input_a(input_a), .input_b(multiplexer_2_out), ._1(Opcode[2]), ._2(Opcode[1]),
    .\output (logic_unit_output));
  Multiplexer #(.width(8)) multiplexer_3 (
    .in0(arthmetic_unit_output), .in1(logic_unit_output), .out(out_8), .sel(Opcode[3]), .en(in_6));

  // Other names for the same wires on the sheet: f0 = Opcode[0]; f1 = Opcode[1]; f2 = Opcode[2]; f3 = Opcode[3]
endmodule
